// Logisim project CRC.circ as structural Verilog: 2 circuits, main circuit CRC
module _4_BITmod2 (
  input  [3:0] A,
  input  [3:0] B,
  output D,
  output [2:0] C
);

  wire [2:0] xor_1_out;

  assign xor_1_out = A[2:0] ^ B[2:0];  // XOR_Gate xor_1, 3 bits wide
  Multiplexer #(.width(3), .enable("false")) multiplexer_1 (.in0(A[2:0]), .in1(xor_1_out), .out(C), .sel(A[3]));

  assign D = A[3];
endmodule

module CRC (
  input  [7:0] A,
  input  [3:0] B,
  output [10:0] C
);

  wire n4_bitmod2_6_p1;
  wire [2:0] n4_bitmod2_1_c, n4_bitmod2_2_c, n4_bitmod2_3_c, n4_bitmod2_4_c, n4_bitmod2_5_c, n4_bitmod2_6_p5,
       n4_bitmod2_7_c;

  _4_BITmod2 u_4_bitmod2_1 (.A(A[7:4]), .B(B), .C(n4_bitmod2_1_c));  // open: D
  _4_BITmod2 u_4_bitmod2_2 (.A({n4_bitmod2_1_c, A[3]}), .B(B), .C(n4_bitmod2_2_c));  // open: D
  _4_BITmod2 u_4_bitmod2_3 (.A({n4_bitmod2_2_c, A[2]}), .B(B), .C(n4_bitmod2_3_c));  // open: D
  _4_BITmod2 u_4_bitmod2_4 (.A({n4_bitmod2_3_c, A[1]}), .B(B), .C(n4_bitmod2_4_c));  // open: D
  _4_BITmod2 u_4_bitmod2_5 (.A({n4_bitmod2_4_c, A[0]}), .B(B), .C(n4_bitmod2_5_c));  // open: D
  // _4_BITmod2 4_bitmod2_6: pin names not known; wires that end beside it: n4_bitmod2_6_p1, {n4_bitmod2_5_c, 1'b0}, B, n4_bitmod2_6_p1, n4_bitmod2_6_p5
  // Probe on {n4_bitmod2_6_p5, 1'b0}
  _4_BITmod2 u_4_bitmod2_7 (.A({n4_bitmod2_6_p5, 1'b0}), .B(B), .C(n4_bitmod2_7_c));  // open: D
  // Probe on {n4_bitmod2_7_c, 1'b0}
  _4_BITmod2 u_4_bitmod2_8 (.A({n4_bitmod2_7_c, 1'b0}), .B(B), .C(C[2:0]));  // open: D

  assign C[10:3] = A;
endmodule
