// Logisim project P30.circ as structural Verilog: 5 circuits, main circuit main
module main (
  input  reset,
  output [31:0] out_2,
  output out_3,
  output [4:0] out_4,
  output [31:0] out_5,
  output out_6,
  output [4:0] out_7,
  output [31:0] out_8
);

  wire alu_1_out_4, branch, clk, controller_1_alusrc, controller_1_branch, controller_1_jump,
       controller_1_left16, controller_1_memtoreg, controller_1_regdst, or_1_out;
  wire [1:0] controller_1_alucontrol;
  wire [31:0] bit_extender_1_out, grf_1_rd1, MemAddr, multiplexer_2_out, multiplexer_4_out, npc_1_npc,
       ram_1_data, register_1_q;

  Clock clock_1 (.out(clk));
  Register #(.width(32)) register_1 (.D(npc_1_npc), .en(1'b1), .Q(register_1_q), .clk(clk), .clr(reset));
  NPC npc_1 (.Branch(branch), .jump(controller_1_jump), .PC(register_1_q), .Instruct(out_2), .NPC(npc_1_npc));
  ROM #(.addrWidth(5), .dataWidth(32)) rom_1 (.addr(register_1_q[6:2]), .data(out_2));  // open: sel
  assign bit_extender_1_out = {{16{1'b0}}, out_2[15:0]};  // Bit_Extender bit_extender_1
  Controller controller_1 (
    .opcode(out_2[31:26]), .Function(out_2[5:0]), .jump(controller_1_jump), .Reg_Write(out_3),
    .RegDst(controller_1_regdst), .ALUSrc(controller_1_alusrc), .Branch(controller_1_branch),
    .MemWrite(out_6), .ALUControl(controller_1_alucontrol), .left16(controller_1_left16),
    .MemtoReg(controller_1_memtoreg));
  GRF grf_1 (
    .in_4(out_2[25:21]), .in_5(out_2[20:16]), .in_6(out_4), .WD(out_5), .RD1(grf_1_rd1), .RD2(out_8),
    .clk(clk), .reset(reset), .WE(out_3));
  Multiplexer #(.width(5), .enable("false")) multiplexer_1 (
    .in0(out_2[20:16]), .in1(out_2[15:11]), .out(out_4), .sel(controller_1_regdst));
  Multiplexer #(.width(32), .enable("false")) multiplexer_2 (
    .in0(out_8), .in1(bit_extender_1_out), .out(multiplexer_2_out), .sel(controller_1_alusrc));
  ALU alu_1 (
    .ALUcontrol(controller_1_alucontrol), .Src1(grf_1_rd1), .Src2(multiplexer_2_out), .out_4(alu_1_out_4),
    .ALUResult({MemAddr[31:7], out_7, MemAddr[1:0]}));
  and PCSrc (branch, controller_1_branch, alu_1_out_4);
  Multiplexer #(.width(32), .enable("false")) multiplexer_3 (
    .in0(multiplexer_4_out), .in1({out_2[15:0], {16{1'b0}}}), .out(out_5), .sel(controller_1_left16));
  or or_1 (or_1_out, out_6, controller_1_memtoreg);
  RAM #(.addrWidth(5), .dataWidth(32), .bus("separate")) ram_1 (
    .addr(out_7), .din(out_8), .data(ram_1_data), .str(out_6), .sel(or_1_out), .clk(clk), .ld(1'b1),
    .clr(reset));
  Multiplexer #(.width(32), .enable("false")) multiplexer_4 (
    .in0({MemAddr[31:7], out_7, MemAddr[1:0]}), .in1(ram_1_data), .out(multiplexer_4_out),
    .sel(controller_1_memtoreg));

  // Other names for the same wires on the sheet: Instr[31:0] = out_2; MemAddr[6:2] = out_7; MemData[31:0] = out_8;
  //   MemWrite = out_6; RegAddr[4:0] = out_4; RegData[31:0] = out_5; RegWrite = out_3

  // Notes on the sheet:
  //   contents of rom_1 (hex, n*v repeats v):
  //   1084023 2318823 1294823 16b5823 20100028 210a0001 11100008 0 1405821 1495021 1604821 ad0a0000
  //   21080004 8100006 0 1084023 3c11ffff 3c010000 3421fffe 2218820 1110000a 0 8d090000 3c0a0100 35290100
  //   12a4825 1314824 ad090028 21080004 8100014 0 8100000
endmodule

module GRF (
  input  clk,
  input  reset,
  input  WE,
  input  [4:0] in_4,
  input  [4:0] in_5,
  input  [4:0] in_6,
  input  [31:0] WD,
  output [31:0] RD1,
  output [31:0] RD2
);

  wire _0r, _1r, _2r, _3r, _4r, _5r, _6r, _7r, _8r, _9r, _10r, _11r, _12r, _13r, _14r, _15r, _16r, _17r,
       _18r, _19r, _20r, _21r, _22r, _23r, _24r, _25r, _26r, _27r, _28r, _29r, _30r, _31r;
  wire [4:0] and_1_out;
  wire [31:0] _0, _1, _2, _3, _4, _5, _6, _7, _8, _9, _10, _11, _12, _13, _14, _15, _16, _17, _18, _19, _20,
       _21, _22, _23, _24, _25, _26, _27, _28, _29, _30, _31;

  Register #(.width(32)) register_1 (.D({32{1'b0}}), .en(1'b1), .Q(_0), .clk(clk), .clr(reset));
  Register #(.width(32)) register_2 (.D(WD), .en(_1r), .Q(_1), .clk(clk), .clr(reset));
  Register #(.width(32)) register_3 (.D(WD), .en(_2r), .Q(_2), .clk(clk), .clr(reset));
  Register #(.width(32)) register_4 (.D(WD), .en(_3r), .Q(_3), .clk(clk), .clr(reset));
  Register #(.width(32)) register_5 (.D(WD), .en(_4r), .Q(_4), .clk(clk), .clr(reset));
  Register #(.width(32)) register_6 (.D(WD), .en(_5r), .Q(_5), .clk(clk), .clr(reset));
  Register #(.width(32)) register_7 (.D(WD), .en(_6r), .Q(_6), .clk(clk), .clr(reset));
  Register #(.width(32)) register_8 (.D(WD), .en(_7r), .Q(_7), .clk(clk), .clr(reset));
  Register #(.width(32)) register_9 (.D(WD), .en(_8r), .Q(_8), .clk(clk), .clr(reset));
  Register #(.width(32)) register_10 (.D(WD), .en(_9r), .Q(_9), .clk(clk), .clr(reset));
  Register #(.width(32)) register_11 (.D(WD), .en(_10r), .Q(_10), .clk(clk), .clr(reset));
  Register #(.width(32)) register_12 (.D(WD), .en(_11r), .Q(_11), .clk(clk), .clr(reset));
  Register #(.width(32)) register_13 (.D(WD), .en(_12r), .Q(_12), .clk(clk), .clr(reset));
  Register #(.width(32)) register_14 (.D(WD), .en(_13r), .Q(_13), .clk(clk), .clr(reset));
  Register #(.width(32)) register_15 (.D(WD), .en(_14r), .Q(_14), .clk(clk), .clr(reset));
  Register #(.width(32)) register_16 (.D(WD), .en(_15r), .Q(_15), .clk(clk), .clr(reset));
  Register #(.width(32)) register_17 (.D(WD), .en(_16r), .Q(_16), .clk(clk), .clr(reset));
  Register #(.width(32)) register_18 (.D(WD), .en(_17r), .Q(_17), .clk(clk), .clr(reset));
  Register #(.width(32)) register_19 (.D(WD), .en(_18r), .Q(_18), .clk(clk), .clr(reset));
  Register #(.width(32)) register_20 (.D(WD), .en(_19r), .Q(_19), .clk(clk), .clr(reset));
  Register #(.width(32)) register_21 (.D(WD), .en(_20r), .Q(_20), .clk(clk), .clr(reset));
  Register #(.width(32)) register_22 (.D(WD), .en(_21r), .Q(_21), .clk(clk), .clr(reset));
  Register #(.width(32)) register_23 (.D(WD), .en(_22r), .Q(_22), .clk(clk), .clr(reset));
  Register #(.width(32)) register_24 (.D(WD), .en(_23r), .Q(_23), .clk(clk), .clr(reset));
  Register #(.width(32)) register_25 (.D(WD), .en(_24r), .Q(_24), .clk(clk), .clr(reset));
  Register #(.width(32)) register_26 (.D(WD), .en(_25r), .Q(_25), .clk(clk), .clr(reset));
  Register #(.width(32)) register_27 (.D(WD), .en(_26r), .Q(_26), .clk(clk), .clr(reset));
  Register #(.width(32)) register_28 (.D(WD), .en(_27r), .Q(_27), .clk(clk), .clr(reset));
  Register #(.width(32)) register_29 (.D(WD), .en(_28r), .Q(_28), .clk(clk), .clr(reset));
  Register #(.width(32)) register_30 (.D(WD), .en(_29r), .Q(_29), .clk(clk), .clr(reset));
  Register #(.width(32)) register_31 (.D(WD), .en(_30r), .Q(_30), .clk(clk), .clr(reset));
  Register #(.width(32)) register_32 (.D(WD), .en(_31r), .Q(_31), .clk(clk), .clr(reset));
  assign and_1_out = in_6 & {5{WE}};  // AND_Gate and_1, 5 bits wide
  Decoder #(.select(5), .enable("false")) decoder_1 (
    .out0(_0r), .out1(_1r), .out2(_2r), .out3(_3r), .out4(_4r), .out5(_5r), .out6(_6r), .out7(_7r),
    .out8(_8r), .out9(_9r), .out10(_10r), .out11(_11r), .out12(_12r), .out13(_13r), .out14(_14r),
    .out15(_15r), .out16(_16r), .out17(_17r), .out18(_18r), .out19(_19r), .out20(_20r), .out21(_21r),
    .out22(_22r), .out23(_23r), .out24(_24r), .out25(_25r), .out26(_26r), .out27(_27r), .out28(_28r),
    .out29(_29r), .out30(_30r), .out31(_31r), .sel(and_1_out));
  Multiplexer #(.select(5), .width(32), .enable("false")) multiplexer_1 (
    .in0(_0), .in1(_1), .in2(_2), .in3(_3), .in4(_4), .in5(_5), .in6(_6), .in7(_7), .in8(_8), .in9(_9),
    .in10(_10), .in11(_11), .in12(_12), .in13(_13), .in14(_14), .in15(_15), .in16(_16), .in17(_17),
    .in18(_18), .in19(_19), .in20(_20), .in21(_21), .in22(_22), .in23(_23), .in24(_24), .in25(_25),
    .in26(_26), .in27(_27), .in28(_28), .in29(_29), .in30(_30), .in31(_31), .out(RD1), .sel(in_4));
  Multiplexer #(.select(5), .width(32), .enable("false")) multiplexer_2 (
    .in0(_0), .in1(_1), .in2(_2), .in3(_3), .in4(_4), .in5(_5), .in6(_6), .in7(_7), .in8(_8), .in9(_9),
    .in10(_10), .in11(_11), .in12(_12), .in13(_13), .in14(_14), .in15(_15), .in16(_16), .in17(_17),
    .in18(_18), .in19(_19), .in20(_20), .in21(_21), .in22(_22), .in23(_23), .in24(_24), .in25(_25),
    .in26(_26), .in27(_27), .in28(_28), .in29(_29), .in30(_30), .in31(_31), .out(RD2), .sel(in_5));

  // Other names for the same wires on the sheet: A1[4:0] = in_4; A2[4:0] = in_5; A3[4:0] = in_6; IN[31:0] = WD
endmodule

module ALU (
  input  [1:0] ALUcontrol,
  input  [31:0] Src1,
  input  [31:0] Src2,
  output out_4,
  output [31:0] ALUResult
);

  wire [31:0] adder_1_out, and_1_out, or_1_out, subtractor_1_out;

  Adder #(.width(32)) adder_1 (.a(Src1), .b(Src2), .out(adder_1_out));  // open: cin, cout
  Subtractor #(.width(32)) subtractor_1 (.a(Src1), .b(Src2), .out(subtractor_1_out));  // open: bin, bout
  assign and_1_out = Src1 & Src2;  // AND_Gate and_1, 32 bits wide
  assign or_1_out = Src1 | Src2;  // OR_Gate or_1, 32 bits wide
  Multiplexer #(.select(2), .width(32), .enable("false")) multiplexer_1 (
    .in0(adder_1_out), .in1(subtractor_1_out), .in2(and_1_out), .in3(or_1_out), .out(ALUResult),
    .sel(ALUcontrol));
  Comparator #(.width(32), .mode("unsigned")) comparator_1 (.a(ALUResult), .b({32{1'b0}}), .eq(out_4));  // open: gt, lt
endmodule

module Controller (
  input  [5:0] opcode,
  input  [5:0] Function,
  output Reg_Write,
  output RegDst,
  output ALUSrc,
  output Branch,
  output MemWrite,
  output [1:0] ALUControl,
  output jump,
  output left16,
  output MemtoReg
);

  wire addi_out, addu_out, and_out, comparator_1_eq, not_1_out, not_2_out, not_3_out, not_4_out, not_5_out,
       not_6_out, not_7_out, not_8_out, not_9_out, not_10_out, not_11_out, not_12_out, or_out, ori_out,
       subu_out;
  wire [1:0] ALUOp, or_2_out;

  not not_1 (not_1_out, Function[0]);
  not not_2 (not_2_out, Function[1]);
  not not_3 (not_3_out, Function[2]);
  not not_4 (not_4_out, Function[3]);
  not not_5 (not_5_out, Function[4]);
  not not_6 (not_6_out, Function[5]);
  and addu (addu_out, Function[5], not_5_out, not_4_out, not_3_out, not_2_out, Function[0]);
  and subu (subu_out, Function[5], not_5_out, not_4_out, not_3_out, Function[1], Function[0]);
  not not_7 (not_7_out, opcode[0]);
  not not_8 (not_8_out, opcode[1]);
  not not_9 (not_9_out, opcode[2]);
  not not_10 (not_10_out, opcode[3]);
  not not_11 (not_11_out, opcode[4]);
  not not_12 (not_12_out, opcode[5]);
  and \or  (or_out, Function[5], not_5_out, not_4_out, Function[2], not_2_out, Function[0]);
  and R (RegDst, not_12_out, not_11_out, not_10_out, not_9_out, not_8_out, not_7_out);
  and \and  (and_out, Function[5], not_5_out, not_4_out, Function[2], not_2_out, not_1_out);
  and ori (ori_out, not_12_out, not_11_out, opcode[3], opcode[2], not_8_out, opcode[0]);
  and lw (MemtoReg, opcode[5], not_11_out, not_10_out, not_9_out, opcode[1], opcode[0]);
  or or_2 (or_2_out[0], or_out, subu_out);
  or or_3 (or_2_out[1], or_out, and_out);
  and sw (MemWrite, opcode[5], not_11_out, opcode[3], not_9_out, opcode[1], opcode[0]);
  and beq (Branch, not_12_out, not_11_out, not_10_out, opcode[2], not_8_out, not_7_out);
  Comparator #(.width(2), .mode("unsigned")) comparator_1 (.a(ALUOp), .b(2'b10), .eq(comparator_1_eq));  // open: gt, lt
  and lui (left16, not_12_out, not_11_out, opcode[3], opcode[2], opcode[1], opcode[0]);
  Multiplexer #(.width(2), .enable("false")) multiplexer_1 (
    .in0(ALUOp), .in1(or_2_out), .out(ALUControl), .sel(comparator_1_eq));
  and addi (addi_out, not_12_out, not_11_out, opcode[3], not_9_out, not_8_out, not_7_out);
  and j (jump, not_12_out, not_11_out, not_10_out, not_9_out, opcode[1], not_7_out);
  or or_4 (ALUOp[0], ori_out, Branch);
  or or_5 (ALUOp[1], ori_out, RegDst);
  or or_6 (Reg_Write, RegDst, ori_out, MemtoReg, left16, addi_out);
  or or_7 (ALUSrc, ori_out, MemtoReg, MemWrite, addi_out);

  // Other names for the same wires on the sheet: f0 = Function[0]; f1 = Function[1]; f2 = Function[2];
  //   f3 = Function[3]; f4 = Function[4]; f5 = Function[5]; op0 = opcode[0]; op1 = opcode[1]; op2 = opcode[2];
  //   op3 = opcode[3]; op4 = opcode[4]; op5 = opcode[5]
endmodule

module NPC (
  input  Branch,
  input  jump,
  input  [31:0] PC,
  input  [31:0] Instruct,
  output [31:0] NPC
);

  wire [25:0] subtractor_1_out;
  wire [27:0] bit_extender_1_out, shifter_1_out;
  wire [31:0] adder_1_out, adder_2_out, bit_extender_2_out, shifter_2_out;

  Subtractor #(.width(26)) subtractor_1 (.a(Instruct[25:0]), .b(26'h3000), .out(subtractor_1_out));  // open: bin, bout
  Adder #(.width(32)) adder_1 (.a(PC), .b(32'h4), .out(adder_1_out));  // open: cin, cout
  assign bit_extender_1_out = {{2{subtractor_1_out[25]}}, subtractor_1_out};  // Bit_Extender bit_extender_1
  assign bit_extender_2_out = {{16{Instruct[15]}}, Instruct[15:0]};  // Bit_Extender bit_extender_2
  Shifter #(.width(28)) shifter_1 (.in(bit_extender_1_out), .\dist (5'b00010), .out(shifter_1_out));
  Shifter #(.width(32)) shifter_2 (.in(bit_extender_2_out), .\dist (5'b00010), .out(shifter_2_out));
  Adder #(.width(32)) adder_2 (.a(adder_1_out), .b(shifter_2_out), .out(adder_2_out));  // open: cin, cout
  Multiplexer #(.select(2), .width(32), .enable("false")) multiplexer_1 (
    .in0(adder_1_out), .in1(adder_2_out), .in2({PC[31:28], shifter_1_out}), .out(NPC), .sel({jump, Branch}));  // open: in3
endmodule
