// Logisim project fsm.circ as structural Verilog: 1 circuit, main circuit fsm
module fsm (
  input  CLR,
  input  [1:0] In,
  output Z
);

  wire _0, _1, _2, _3, and_3_out, and_4_out, and_8_out, and_9_out, and_10_out, clock_1_out, clr_t, l1, l2,
       l3, l4, l5, l6, not_2_out, not_4_out, not_5_out, not_6_out, not_8_out, or_5_out, register_1_q, S0, S1,
       S2, S3;

  not not_1 (clr_t, CLR);
  not not_2 (not_2_out, In[1]);
  and and_1 (l1, In[0], In[1]);
  not not_3 (l2, l3);
  and and_2 (l3, In[0], not_2_out);
  or or_1 (l4, S1, S2, S3);
  or or_2 (l5, S3, S0);
  or or_3 (l6, l4, S0);
  not not_4 (not_4_out, In[0]);
  and and_3 (and_3_out, l5, l2);
  or or_4 (_0, and_3_out, and_4_out);
  and and_4 (and_4_out, l1, l4);
  and and_5 (_1, l6, l3);
  and and_6 (_2, S1, not_4_out);
  and and_7 (_3, not_4_out, S2);
  not not_5 (not_5_out, clr_t);
  or or_5 (or_5_out, not_5_out, _0);
  and and_8 (and_8_out, _1, clr_t);
  and and_9 (and_9_out, _2, clr_t);
  and and_10 (and_10_out, _3, clr_t);
  Clock clock_1 (.out(clock_1_out));
  not not_6 (not_6_out, or_5_out);
  Register #(.width(1)) register_1 (.D(not_6_out), .en(1'b1), .Q(register_1_q), .clk(clock_1_out));  // open: clr
  Register #(.width(1)) register_2 (.D(and_8_out), .en(1'b1), .Q(S1), .clk(clock_1_out));  // open: clr
  Register #(.width(1)) register_3 (.D(and_9_out), .en(1'b1), .Q(S2), .clk(clock_1_out));  // open: clr
  Register #(.width(1)) register_4 (.D(and_10_out), .en(1'b1), .Q(S3), .clk(clock_1_out));  // open: clr
  not not_7 (S0, register_1_q);
  not not_8 (not_8_out, In[0]);
  and and_11 (Z, not_8_out, S2);

  // Other names for the same wires on the sheet: A2 = In[0]; A1 = In[1]
endmodule
