// Logisim project ftoi.circ as structural Verilog: 1 circuit, main circuit ftoi
module ftoi (
  input  [15:0] in_1,
  output [31:0] out_2
);

  wire comparator_1_eq, comparator_2_eq, comparator_2_gt, or_1_out;
  wire [3:0] subtractor_2_out, subtractor_3_out;
  wire [4:0] subtractor_1_out;
  wire [10:0] multiplexer_1_out;
  wire [15:0] multiplexer_2_out, shifter_1_out, shifter_2_out;
  wire [30:0] not_1_out;
  wire [31:0] adder_1_out, multiplexer_3_out;

  // Probe on 5'b01111
  Comparator #(.width(5)) comparator_1 (.a({5{1'b0}}), .b(in_1[14:10]), .eq(comparator_1_eq));  // open: gt, lt
  Subtractor #(.width(5)) subtractor_1 (.a(in_1[14:10]), .b(5'b01111), .out(subtractor_1_out));  // open: bin, bout
  Multiplexer #(.width(11), .enable("false")) multiplexer_1 (
    .in0({1'b1, in_1[9:0]}), .in1({1'b0, in_1[9:0]}), .out(multiplexer_1_out), .sel(comparator_1_eq));
  Comparator #(.width(4), .mode("unsigned")) comparator_2 (
    .a(4'b1010), .b(subtractor_1_out[3:0]), .gt(comparator_2_gt), .eq(comparator_2_eq));  // open: lt
  // Probe on subtractor_1_out[3:0]
  // Probe on {{5{1'b0}}, multiplexer_1_out}
  Subtractor #(.width(4)) subtractor_2 (
    .a(subtractor_1_out[3:0]), .b(4'b1010), .out(subtractor_2_out));  // open: bin, bout
  Subtractor #(.width(4)) subtractor_3 (
    .a(4'b1010), .b(subtractor_1_out[3:0]), .out(subtractor_3_out));  // open: bin, bout
  or or_1 (or_1_out, comparator_2_gt, comparator_2_eq);
  Shifter #(.width(16)) shifter_1 (.in({{5{1'b0}}, multiplexer_1_out}), .\dist (subtractor_2_out), .out(shifter_1_out));
  Shifter #(.width(16), .shift("lr")) shifter_2 (
    .in({{5{1'b0}}, multiplexer_1_out}), .\dist (subtractor_3_out), .out(shifter_2_out));
  Multiplexer #(.width(16), .enable("false")) multiplexer_2 (
    .in0(shifter_1_out), .in1(shifter_2_out), .out(multiplexer_2_out), .sel(or_1_out));
  assign not_1_out = ~{{15{1'b0}}, multiplexer_2_out};  // NOT_Gate not_1, 31 bits wide
  Adder #(.width(32)) adder_1 (.a({in_1[15], not_1_out}), .b(32'h1), .out(adder_1_out));  // open: cin, cout
  Multiplexer #(.width(32), .enable("false")) multiplexer_3 (
    .in0({in_1[15], {15{1'b0}}, multiplexer_2_out}), .in1(adder_1_out), .out(multiplexer_3_out),
    .sel(in_1[15]));
  Multiplexer #(.width(32), .enable("false")) multiplexer_4 (
    .in0(multiplexer_3_out), .in1({32{1'b0}}), .out(out_2), .sel(subtractor_1_out[4]));
endmodule
