// Logisim project grf.circ as structural Verilog: 1 circuit, main circuit grf
module grf (
  input  clk,
  input  reset,
  input  WE,
  input  [4:0] A1,
  input  [4:0] A2,
  input  [4:0] A3,
  input  [31:0] WD,
  output [31:0] out_8,
  output [31:0] out_9
);

  wire _1r, _2r, _3r, _4r, _5r, _6r, _7r, _8r, _9r, _10r, _11r, _12r, _13r, _14r, _15r, _16r, _17r, _18r,
       _19r, _20r, _21r, _22r, _23r, _24r, _25r, _26r, _27r, _28r, _29r, _30r, _31r, _32r;
  wire [4:0] and_1_out;
  wire [31:0] _1, _2, _3, _4, _5, _6, _7, _8, _9, _10, _11, _12, _13, _14, _15, _16, _17, _18, _19, _20, _21,
       _22, _23, _24, _25, _26, _27, _28, _29, _30, _31, _32;

  assign and_1_out = A3 & {5{WE}};  // AND_Gate and_1, 5 bits wide
  Decoder #(.select(5), .enable("false")) decoder_1 (
    .out0(_1r), .out1(_2r), .out2(_3r), .out3(_4r), .out4(_5r), .out5(_6r), .out6(_7r), .out7(_8r),
    .out8(_9r), .out9(_10r), .out10(_11r), .out11(_12r), .out12(_13r), .out13(_14r), .out14(_15r),
    .out15(_16r), .out16(_17r), .out17(_18r), .out18(_19r), .out19(_20r), .out20(_21r), .out21(_22r),
    .out22(_23r), .out23(_24r), .out24(_25r), .out25(_26r), .out26(_27r), .out27(_28r), .out28(_29r),
    .out29(_30r), .out30(_31r), .out31(_32r), .sel(and_1_out));
  Register #(.width(32)) register_1 (.D({32{1'b0}}), .en(1'b1), .Q(_1), .clk(clk), .clr(reset));
  Register #(.width(32)) register_2 (.D(WD), .en(_2r), .Q(_2), .clk(clk), .clr(reset));
  Register #(.width(32)) register_3 (.D(WD), .en(_3r), .Q(_3), .clk(clk), .clr(reset));
  Register #(.width(32)) register_4 (.D(WD), .en(_4r), .Q(_4), .clk(clk), .clr(reset));
  Register #(.width(32)) register_5 (.D(WD), .en(_5r), .Q(_5), .clk(clk), .clr(reset));
  Register #(.width(32)) register_6 (.D(WD), .en(_6r), .Q(_6), .clk(clk), .clr(reset));
  Register #(.width(32)) register_7 (.D(WD), .en(_7r), .Q(_7), .clk(clk), .clr(reset));
  Register #(.width(32)) register_8 (.D(WD), .en(_8r), .Q(_8), .clk(clk), .clr(reset));
  Register #(.width(32)) register_9 (.D(WD), .en(_9r), .Q(_9), .clk(clk), .clr(reset));
  Register #(.width(32)) register_10 (.D(WD), .en(_10r), .Q(_10), .clk(clk), .clr(reset));
  Register #(.width(32)) register_11 (.D(WD), .en(_11r), .Q(_11), .clk(clk), .clr(reset));
  Register #(.width(32)) register_12 (.D(WD), .en(_12r), .Q(_12), .clk(clk), .clr(reset));
  Register #(.width(32)) register_13 (.D(WD), .en(_13r), .Q(_13), .clk(clk), .clr(reset));
  Register #(.width(32)) register_14 (.D(WD), .en(_14r), .Q(_14), .clk(clk), .clr(reset));
  Register #(.width(32)) register_15 (.D(WD), .en(_15r), .Q(_15), .clk(clk), .clr(reset));
  Register #(.width(32)) register_16 (.D(WD), .en(_16r), .Q(_16), .clk(clk), .clr(reset));
  Multiplexer #(.select(5), .width(32), .enable("false")) multiplexer_1 (
    .in0(_1), .in1(_2), .in2(_3), .in3(_4), .in4(_5), .in5(_6), .in6(_7), .in7(_8), .in8(_9), .in9(_10),
    .in10(_11), .in11(_12), .in12(_13), .in13(_14), .in14(_15), .in15(_16), .in16(_17), .in17(_18),
    .in18(_19), .in19(_20), .in20(_21), .in21(_22), .in22(_23), .in23(_24), .in24(_25), .in25(_26),
    .in26(_27), .in27(_28), .in28(_29), .in29(_30), .in30(_31), .in31(_32), .out(out_8), .sel(A1));
  Register #(.width(32)) register_17 (.D(WD), .en(_17r), .Q(_17), .clk(clk), .clr(reset));
  Register #(.width(32)) register_18 (.D(WD), .en(_18r), .Q(_18), .clk(clk), .clr(reset));
  Register #(.width(32)) register_19 (.D(WD), .en(_19r), .Q(_19), .clk(clk), .clr(reset));
  Register #(.width(32)) register_20 (.D(WD), .en(_20r), .Q(_20), .clk(clk), .clr(reset));
  Register #(.width(32)) register_21 (.D(WD), .en(_21r), .Q(_21), .clk(clk), .clr(reset));
  Register #(.width(32)) register_22 (.D(WD), .en(_22r), .Q(_22), .clk(clk), .clr(reset));
  Register #(.width(32)) register_23 (.D(WD), .en(_23r), .Q(_23), .clk(clk), .clr(reset));
  Register #(.width(32)) register_24 (.D(WD), .en(_24r), .Q(_24), .clk(clk), .clr(reset));
  Multiplexer #(.select(5), .width(32), .enable("false")) multiplexer_2 (
    .in0(_1), .in1(_2), .in2(_3), .in3(_4), .in4(_5), .in5(_6), .in6(_7), .in7(_8), .in8(_9), .in9(_10),
    .in10(_11), .in11(_12), .in12(_13), .in13(_14), .in14(_15), .in15(_16), .in16(_17), .in17(_18),
    .in18(_19), .in19(_20), .in20(_21), .in21(_22), .in22(_23), .in23(_24), .in24(_25), .in25(_26),
    .in26(_27), .in27(_28), .in28(_29), .in29(_30), .in30(_31), .in31(_32), .out(out_9), .sel(A2));
  Register #(.width(32)) register_25 (.D(WD), .en(_25r), .Q(_25), .clk(clk), .clr(reset));
  Register #(.width(32)) register_26 (.D(WD), .en(_26r), .Q(_26), .clk(clk), .clr(reset));
  Register #(.width(32)) register_27 (.D(WD), .en(_27r), .Q(_27), .clk(clk), .clr(reset));
  Register #(.width(32)) register_28 (.D(WD), .en(_28r), .Q(_28), .clk(clk), .clr(reset));
  Register #(.width(32)) register_29 (.D(WD), .en(_29r), .Q(_29), .clk(clk), .clr(reset));
  Register #(.width(32)) register_30 (.D(WD), .en(_30r), .Q(_30), .clk(clk), .clr(reset));
  Register #(.width(32)) register_31 (.D(WD), .en(_31r), .Q(_31), .clk(clk), .clr(reset));
  Register #(.width(32)) register_32 (.D(WD), .en(_32r), .Q(_32), .clk(clk), .clr(reset));

  // Other names for the same wires on the sheet: IN[31:0] = WD; RD1[31:0] = out_8; RD2[31:0] = out_9
endmodule
