// Logisim project navigation.circ as structural Verilog: 1 circuit, main circuit navigation
module navigation (
  input  [1:0] dir,
  input  reset,
  output out_3,
  output out_4
);

  wire _0, _1, _2, _3, _4, _5, and_1_out, and_2_out, and_3_out, and_4_out, and_5_out, and_6_out, and_7_out,
       and_8_out, and_9_out, and_10_out, and_11_out, and_12_out, and_13_out, and_14_out, and_15_out,
       and_16_out, and_17_out, and_18_out, and_19_out, and_20_out, and_21_out, and_22_out, clk, NN1, NN2,
       not_3_out, register_1_q, S0, S1, S2, S3;

  Clock clock_1 (.out(clk));
  not not_1 (NN2, dir[0]);
  not not_2 (NN1, dir[1]);
  and and_1 (and_1_out, NN2, dir[1], S1);
  and and_2 (and_2_out, S0, dir[1]);
  and and_3 (and_3_out, S0, dir[0]);
  and and_4 (and_4_out, NN2, NN1, S0);
  and and_5 (and_5_out, dir[1], NN2, S2);
  and and_6 (and_6_out, dir[1], dir[0], S3);
  and and_7 (and_7_out, dir[1], dir[0], S1);
  and and_8 (and_8_out, dir[1], dir[0], S2);
  and and_9 (and_9_out, NN1, NN2, S2);
  and and_10 (and_10_out, NN1, NN2, S1);
  or or_1 (_0, and_1_out, and_2_out, and_3_out, out_3);
  or or_2 (_1, and_4_out, and_5_out, and_6_out, and_7_out);
  or or_3 (_2, and_8_out, and_9_out, and_10_out);
  and and_11 (and_11_out, NN1, dir[0], S1);
  and and_12 (and_12_out, S3, dir[1], NN2);
  and and_13 (and_13_out, NN1, dir[0], S3);
  and and_14 (and_14_out, NN1, dir[0], S2);
  or or_4 (_4, and_14_out, and_15_out);
  and and_15 (and_15_out, NN1, S3, NN2);
  and and_16 (and_16_out, S3, dir[1], NN2);
  and and_17 (and_17_out, NN1, dir[0], S3);
  and and_18 (and_18_out, dir[1], dir[0], S2);
  and and_19 (and_19_out, NN1, NN2, S2);
  and and_20 (and_20_out, dir[1], dir[0], S1);
  and and_21 (and_21_out, S0, dir[0]);
  and and_22 (and_22_out, S0, dir[1]);
  or or_5 (_3, and_11_out, and_12_out, and_13_out);
  or or_6 (_5, and_16_out, and_17_out, and_18_out, and_19_out, and_20_out, and_21_out, and_22_out);
  not not_3 (not_3_out, _0);
  Register #(.width(1)) register_1 (.D(not_3_out), .en(1'b1), .Q(register_1_q), .clk(clk), .clr(reset));
  not not_4 (S0, register_1_q);
  Register #(.width(1)) register_2 (.D(_1), .en(1'b1), .Q(S1), .clk(clk), .clr(reset));
  Register #(.width(1)) register_3 (.D(_2), .en(1'b1), .Q(S2), .clk(clk), .clr(reset));
  Register #(.width(1)) register_4 (.D(_3), .en(1'b1), .Q(S3), .clk(clk), .clr(reset));
  Register #(.width(1)) register_5 (.D(_4), .en(1'b1), .Q(out_3), .clk(clk), .clr(reset));
  Register #(.width(1)) register_6 (.D(_5), .en(1'b1), .Q(out_4), .clk(clk), .clr(reset));

  // Other names for the same wires on the sheet: N2 = dir[0]; N1 = dir[1]; hit = out_4; S4 = out_3
endmodule
